# Fritzing sketch 3colourLED_wiring (saved by Fritzing 0.8.5b)

parts:
  Raspberry_Pi_1 = Raspberry Pi 3
  LED1 = RGB LED (com. anode, rbg) [package="5 mm [THT]"]
  R1 = Resistor [tolerance=±5% resistance=220 package=THT]
  R2 = Resistor [tolerance=±5% resistance=220 package=THT]
  R3 = Resistor [tolerance=±5% resistance=220 package=THT]

nets:
  N1: Raspberry_Pi_1.GND, LED1.common_anode
  N2: Raspberry_Pi_1.GIPO17, R3.Pin_1
  N3: Raspberry_Pi_1.GIPO27, R2.Pin_1
  N4: Raspberry_Pi_1.GIPO22, R1.Pin_1
  N5: LED1.red_cathode, R3.Pin_0
  N6: LED1.blue_cathode, R2.Pin_0
  N7: LED1.green_cathode, R1.Pin_0
